# Fritzing sketch light dimmer (saved by Fritzing 0.9.6b)
circuit board: 8.46667cm x 5.64444cm
breadboards: 1

parts:
  R2 = Resistor [tolerance=±5% power=0.25 resistance=15 package=THT]
  C1 = Capacitor Polarized [package=panasonic_d]
  C2 = Capacitor Polarized [package=panasonic_d]
  LED1 = LED - 3mm [color="Red (633nm)" current=350 package="3 mm [THT]"]
  S = SWITCH-MOMENTARY-2 [package=tactile-switch-1101ne]
  R1 = TRIMPOT [part_number=50K package=trimpot_pth_s3_lock]
  LED2 = Super Flux LED blue [color=Blue]
  U1 = TRIAC [package=to-92]  # not connected

nets (from the schematic view):
  N1: R2.Pin_0, C1.+, R1.WIPER, R1.CW
  N2: R2.Pin_1, C2.+, LED2.cathode
  N3: C1.-, C2.-, S.2
  N4: LED1.cathode, R1.CCW
  N5: LED1.anode, S.1
